# Fritzing sketch arduino-tools-flash-nano-with-uno (saved by Fritzing 0.9.3b)

parts:
  PROGRAMMER = Arduino Uno (Rev3)
  TARGET = Arduino Nano (Rev3.0) (ICSP)
  C1 = Capacitor Polarized [package=cpol-radial-10uf-25v]

nets:
  N1: PROGRAMMER.D10_PWM/SS, TARGET.RESET
  N2: PROGRAMMER.D11_PWM/MOSI, TARGET.D11/MOSI
  N3: PROGRAMMER.D12/MISO, TARGET.D12/MISO
  N4: PROGRAMMER.D13/SCK, TARGET.D13/SCK
  GND: PROGRAMMER.GND, TARGET.GND, C1.-
  N5: PROGRAMMER.RESET, C1.+
  5V: PROGRAMMER.5V, TARGET.5V
